# Fritzing sketch gpio_midi (saved by Fritzing 0.9.3b)
breadboards: 1

parts:
  R1 = Resistor [tolerance=±5% resistance=220 package="0402 [SMD]"]
  D1 = Rectifier Diode [part_number=1N4148 package="300 mil [THT]"]
  R2 = Resistor [tolerance=±5% resistance=10k package="0402 [SMD]"]
  R3 = Resistor [tolerance=±5% resistance=1k package="0402 [SMD]"]
  Raspberry_Pi = Raspberry Pi 3 [part_number=RPI-3-V1.2]
  IC1 = IC, DIP package, 8 pins [chip_label=6N138]
  U1 = MIDI_CONN_FEMALE_FIXED [package=din_5_female]

nets:
  N1: R1.Pin_0, U1.MIDI_IN
  N2: R1.Pin_1, D1.cathode, IC1.pin2
  N3: D1.anode, IC1.pin3, U1.MIDI_OUT
  N4: R2.Pin_0, IC1.pin7
  N5: R2.Pin_1, Raspberry_Pi.GND, IC1.pin5
  N6: R3.Pin_0, Raspberry_Pi.3v3, IC1.pin8
  N7: R3.Pin_1, Raspberry_Pi.GPIO15, IC1.pin6

custom parts:
  MIDI_CONN_FEMALE_FIXED: MIDI connector, no strain relieve (DIN-5 female) Fixed physical pin assignment for breadboard.
